// Logisim project Project_3.circ as structural Verilog
module main (
  input  in_1
);

  wire n7_segment_display_driver_1_p6, n7_segment_display_driver_1_p7, n7_segment_display_driver_1_p8,
       n7_segment_display_driver_1_p9, n7_segment_display_driver_1_p10, n7_segment_display_driver_1_p11,
       n7_segment_display_driver_1_p12, test_1_out_2, test_1_out_3, test_1_out_4, test_1_out_5;

  test test_1 (.out_2(test_1_out_2), .out_3(test_1_out_3), .out_4(test_1_out_4), .out_5(test_1_out_5));  // open: in_1
  // _7_segment_display_driver 7_segment_display_driver_1: pin names not known; wires that end beside it: in_1, test_1_out_5, test_1_out_4, test_1_out_3, test_1_out_2, n7_segment_display_driver_1_p6, n7_segment_display_driver_1_p7, n7_segment_display_driver_1_p8, n7_segment_display_driver_1_p9, n7_segment_display_driver_1_p10, n7_segment_display_driver_1_p11, n7_segment_display_driver_1_p12
  _7_Segment_Display u_7_segment_display_1 ();  // open: g, f, a, b, e, d, c, dp
  _7_Segment_Display u_7_segment_display_2 (
    .g(n7_segment_display_driver_1_p12), .f(n7_segment_display_driver_1_p11),
    .a(n7_segment_display_driver_1_p6), .b(n7_segment_display_driver_1_p7),
    .e(n7_segment_display_driver_1_p10), .d(n7_segment_display_driver_1_p9),
    .c(n7_segment_display_driver_1_p8));  // open: dp
endmodule

module base_10_up_down_counter (
  input  x_input,
  output s_0,
  output s_1,
  output s_2,
  output s_3
);

  wire and_1_out, clock_1_out, j_k_ff_1_q, j_k_ff_2_q, j_k_ff_3_q, undriven, undriven_2;

  and and_1 (and_1_out, s_3, s_1);
  Clock clock_1 (.out(clock_1_out));
  J_K_Flip_Flop j_k_ff_1 (
    .J(1'b1), .clk(clock_1_out), .K(1'b1), .Q(j_k_ff_1_q), .Qn(s_0), .preset(undriven), .en(undriven),
    .reset(undriven_2));
  J_K_Flip_Flop j_k_ff_2 (
    .J(1'b1), .clk(j_k_ff_1_q), .K(1'b1), .Q(j_k_ff_2_q), .Qn(s_1), .reset(undriven_2));  // open: preset, en
  J_K_Flip_Flop j_k_ff_3 (
    .J(1'b1), .clk(j_k_ff_2_q), .K(1'b1), .Q(j_k_ff_3_q), .Qn(s_2), .reset(undriven_2));  // open: preset, en
  J_K_Flip_Flop j_k_ff_4 (.J(1'b1), .clk(j_k_ff_3_q), .K(1'b1), .Qn(s_3), .reset(undriven_2));  // open: Q, preset, en
endmodule

module test (
  input  in_1,
  output out_2,
  output out_3,
  output out_4,
  output out_5
);

  wire and_1_out, clock_1_out, j_k_ff_1_qn, j_k_ff_2_qn, j_k_ff_3_qn;

  and and_1 (and_1_out, out_5, out_3);
  Clock clock_1 (.out(clock_1_out));
  J_K_Flip_Flop j_k_ff_1 (
    .J(in_1), .clk(clock_1_out), .K(in_1), .Q(out_2), .Qn(j_k_ff_1_qn), .reset(and_1_out));  // open: preset, en
  J_K_Flip_Flop j_k_ff_2 (
    .J(in_1), .clk(j_k_ff_1_qn), .K(in_1), .Q(out_3), .Qn(j_k_ff_2_qn), .reset(and_1_out));  // open: preset, en
  J_K_Flip_Flop j_k_ff_3 (
    .J(in_1), .clk(j_k_ff_2_qn), .K(in_1), .Q(out_4), .Qn(j_k_ff_3_qn), .reset(and_1_out));  // open: preset, en
  J_K_Flip_Flop j_k_ff_4 (.J(in_1), .clk(j_k_ff_3_qn), .K(in_1), .Q(out_5), .reset(and_1_out));  // open: Qn, preset, en
endmodule
